# Fritzing sketch schematic (saved by Fritzing 0.9.6b)

parts:
  Part1 = Thumb Joystick
  Launchpad1 = TI Launchpad MSP430G2

nets:
  N1: Part1.GND, Launchpad1.p20
  N2: Part1.HORZ, Launchpad1.p14
  N3: Part1.VERT, Launchpad1.p15
  N4: Part1.VCC, Launchpad1.p1

notes:
  PWM X Output
  PWM Y Output
